# Fritzing sketch Mama FYP (saved by Fritzing 0.9.3b)
breadboards: 2

parts:
  LED1 = LED - 5mm [color="Red (633nm)" package="5 mm [THT]"]
  J1 = Piezo Speaker
  J2 = Basic Force Sensing Resistor (FSR) [package=THT]
  J3 = Basic Force Sensing Resistor (FSR) [package=THT]
  Part1 = Arduino Uno (Rev3)
  R1 = Resistor [tolerance=±5% resistance=220 package=THT]
  R2 = Resistor [tolerance=±5% resistance=220 package=THT]

nets:
  N1: LED1.cathode, Part1.D6_PWM
  N2: LED1.anode, J1.pin2, Part1.GND, R1.Pin_0, R2.Pin_1
  N3: J1.pin1, Part1.D5_PWM
  N4: J2.pin_0, J3.pin_0, Part1.5V
  N5: J2.pin_1, Part1.A0, R2.Pin_0
  N6: J3.pin_1, Part1.A1, R1.Pin_1

// code stored in the sketch: Mama FYP Code.ino
#define FORCE_SENSOR_PIN1 A0
#define FORCE_SENSOR_PIN2 A1

void setup() 
{
  Serial.begin(9600);
}

void loop() 
{
  int analogReading = analogRead(FORCE_SENSOR_PIN1);

  Serial.print("Force sensor reading = ");
  Serial.print(analogReading); // print the raw analog reading

  if (analogReading < 10)       // from 0 to 9
    Serial.println(" -> no pressure");
  else if (analogReading < 200) // from 10 to 199
    Serial.println(" -> light touch");
  else if (analogReading < 500) // from 200 to 499
    Serial.println(" -> light squeeze");
  else if (analogReading < 800) // from 500 to 799
    Serial.println(" -> medium squeeze");
  else // from 800 to 1023
    Serial.println(" -> big squeeze");

  delay(1000);

  int analogReading = analogRead(FORCE_SENSOR_PIN2);

  Serial.print("Force sensor reading = ");
  Serial.print(analogReading); // print the raw analog reading

  if (analogReading < 10)       // from 0 to 9
    Serial.println(" -> no pressure");
  else if (analogReading < 200) // from 10 to 199
    Serial.println(" -> light touch");
  else if (analogReading < 500) // from 200 to 499
    Serial.println(" -> light squeeze");
  else if (analogReading < 800) // from 500 to 799
    Serial.println(" -> medium squeeze");
  else // from 800 to 1023
    Serial.println(" -> big squeeze");

  delay(1000);
}
